# Fritzing sketch CGScale (saved by Fritzing 0.9.3b)

parts:
  WeMos_D1_Mini1 = WeMos D1 Mini
  HX711_Back = HX711 Weighing Sensor Module [part_number=1]
  HX711_Front = HX711 Weighing Sensor Module

nets:
  VCC: WeMos_D1_Mini1.3V3, HX711_Back.VCC, HX711_Front.VCC
  N1: WeMos_D1_Mini1.D1, HX711_Back.CK/TX
  N2: WeMos_D1_Mini1.D2, HX711_Back.DO/RX
  N3: WeMos_D1_Mini1.D5, HX711_Front.CK/TX
  N4: WeMos_D1_Mini1.D6, HX711_Front.DO/RX
  GND: WeMos_D1_Mini1.G, HX711_Back.GND, HX711_Front.GND
